// Digital circuit ALU.dig as structural Verilog
module ALU (
  input  [15:0] Left,
  input  [15:0] Right,
  output [15:0] result
);

  Add #(.Bits(16)) add_1 (.a(Left), .b(Right), .c_i(1'b0), .s(result));  // open: c_o
endmodule
