// Digital circuit Decoder.dig as structural Verilog
module Decoder (
  input  [15:0] instruction,
  output [3:0] opcode,
  output [1:0] rs,
  output [1:0] rt,
  output [7:0] immediate
);


  assign immediate = instruction[7:0];
  assign opcode = instruction[15:12];
  assign rs = instruction[11:10];
  assign rt = instruction[9:8];
endmodule
